# Fritzing sketch TOFsensorDesign (saved by Fritzing 0.9.3b)
circuit board: 2.28727cm x 2.03426cm
breadboards: 1

parts:
  J1 = female pin header, 4 pins [form="♀ (female)"]
  J2 = female pin header, 6 pins [form="♀ (female)"]

nets:
  N1: J1.pin1, J2.pin3
  N2: J1.pin2, J2.pin4
  N3: J1.pin3, J2.pin5
  N4: J1.pin4, J2.pin1, J2.pin6

notes:
  VCC
  GND
  SDA
  SCL
  J1
  VL53L0X
  GPIO1
  XSHUT
  B Woo
